// Digital circuit Memory.dig as structural Verilog
module Memory (
  input  [31:0] PC,
  input  [31:0] Data_in,
  input  [31:0] Addr,
  input  C,
  input  str,
  output [31:0] Instr,
  output [31:0] Data_out
);

  wire comparator_1_eq, comparator_2_eq;
  wire [31:0] ramdualaccess_1_d1, ramdualaccess_1_d2;

  Comparator #(.Bits(8)) comparator_1 (.a({8{1'b0}}), .b(Addr[31:24]), .eq(comparator_1_eq));  // open: gt, lt
  Comparator #(.Bits(8)) comparator_2 (.a(PC[31:24]), .b({8{1'b0}}), .eq(comparator_2_eq));  // open: gt, lt
  RAMDualAccess #(.AddrBits(24), .isProgramMemory("true"), .Bits(32)) ramdualaccess_1 (
    .str(str), .C(C), .ld(1'b1), .A1(Addr[23:0]), .Din1(Data_in), .A2(PC[23:0]), .D1(ramdualaccess_1_d1),
    .D2(ramdualaccess_1_d2));
  Multiplexer #(.Bits(32)) multiplexer_1 (
    .sel(comparator_1_eq), .in_0({32{1'b0}}), .in_1(ramdualaccess_1_d1), .out(Data_out));
  Multiplexer #(.Bits(32)) multiplexer_2 (
    .sel(comparator_2_eq), .in_0({32{1'b0}}), .in_1(ramdualaccess_1_d2), .out(Instr));
endmodule

/* Test case Write one cell:
C str Addr Data_in PC Data_out Instr
0 0   0    0       0  0        0
0 0   1    0       0  0        0
0 0   0    0       1  0        0
C 0   0    5       1  0        0
0 1   0    5       1  0        0
C 1   0    5       1  5        0
0 0   1    0       0  0        5
C 1   0    0       0  0        0
*/

/* Test case Write full RAM:
	C str Addr       Data_in PC       Data_out Instr
# Write some of the RAM
loop(a, 1<<16)
	0 0   (a << 8)   (a + 5) (-1)     0        0
	C 1   (a << 8)   (a + 5) (-1)     (a + 5)  0
end loop

# Read the data through Addr
loop(a, 1<<16)
	0 0   (a << 8)   0       (-1)     (a + 5)  0
end loop

# Read the data through PC
loop(a, 1<<16)
	0 0   0xFFFFFFFF 0       (a << 8) 0       (a + 5)
end loop
*/

/* Test case Out of range:
	C str Addr Data_in    PC Data_out Instr
# Write random addresses
loop(i, 10000)
	# Generate random addresss >= (1 << 24)
	let a = (((random(7) + 1) << 24) + random(1 << 24));

	0 0   (a)  0x5A5A5A5A 0  0        0
	C 1   (a)  0x5A5A5A5A 0  0        0
end loop
*/

/* Test case Preload program:
	C str Addr Data_in PC   Data_out   Instr
program(0x5A5A5A5A, 0xA5A5A5A5, 0x0, 0x1, 0xFFFFFFFF)
	0 0   0    0       (-1) 0x5A5A5A5A 0
	0 0   1    0       (-1) 0xA5A5A5A5 0
	0 0   2    0       (-1) 0x0        0
	0 0   3    0       (-1) 0x1        0
	0 0   4    0       (-1) 0xFFFFFFFF 0
	0 0   5    0       (-1) 0          0
*/
