// Digital circuit PC.dig as structural Verilog
module PC (
  input  C,
  output [31:0] PC
);

  CounterPreset #(.Bits(30), .isProgramCounter("true")) counterpreset_1 (
    .en(1'b1), .C(C), .dir(1'b0), .in({30{1'b0}}), .ld(1'b0), .clr(1'b0), .out(PC[31:2]));  // open: ovf

  assign PC[1:0] = 2'b00;
endmodule
